// Logisim project Somador.circ as structural Verilog: 10 circuits, main circuit main
module main (
  input  in_1,
  input  in_2,
  input  in_3,
  input  in_4,
  input  in_5,
  input  in_6,
  output out_7,
  output out_8,
  output out_9,
  output out_10
);

  wire db_1_out_5, db_2_out_5, db_3_out_5, \dc_1_saída , \dc_2_saída , \dc_3_saída , \dezenas_1_saída ,
       \eb_1_saída , \eb_2_saída , \eb_3_saída , \ec_1_saída , \ec_2_saída , \ec_3_saída , \mb_1_saída ,
       \mb_2_saída , \mb_3_saída , \mc_1_saída , \mc_2_saída , \mc_3_saída , \mm_1_saída , \mm_2_saída ,
       \mm_3_saída , soma_1_vai1, soma_2_vai1;

  DC dc_1 (.A(1'b0), .B(in_1), .C(in_2), .D(in_3), .\Saída (\dc_1_saída ));
  MC mc_1 (.A(1'b0), .B(in_1), .C(in_2), .D(in_3), .\Saída (\mc_1_saída ));
  EC ec_1 (.A(1'b0), .B(in_1), .C(in_2), .D(in_3), .\Saída (\ec_1_saída ));
  MM mm_1 (.A(1'b0), .B(in_1), .C(in_2), .D(in_3), .\Saída (\mm_1_saída ));
  EB eb_1 (.A(1'b0), .B(in_1), .C(in_2), .D(in_3), .\Saída (\eb_1_saída ));
  MB mb_1 (.A(1'b0), .B(in_1), .C(in_2), .D(in_3), .\Saída (\mb_1_saída ));
  DB db_1 (.A(1'b0), .B(in_1), .C(in_2), .D(in_3), .out_5(db_1_out_5));
  DC dc_2 (.A(1'b0), .B(in_4), .C(in_5), .D(in_6), .\Saída (\dc_2_saída ));
  MC mc_2 (.A(1'b0), .B(in_4), .C(in_5), .D(in_6), .\Saída (\mc_2_saída ));
  EC ec_2 (.A(1'b0), .B(in_4), .C(in_5), .D(in_6), .\Saída (\ec_2_saída ));
  MM mm_2 (.A(1'b0), .B(in_4), .C(in_5), .D(in_6), .\Saída (\mm_2_saída ));
  EB eb_2 (.A(1'b0), .B(in_4), .C(in_5), .D(in_6), .\Saída (\eb_2_saída ));
  MB mb_2 (.A(1'b0), .B(in_4), .C(in_5), .D(in_6), .\Saída (\mb_2_saída ));
  DB db_2 (.A(1'b0), .B(in_4), .C(in_5), .D(in_6), .out_5(db_2_out_5));
  Soma soma_1 (.bit1(in_3), .bit2(in_6), .Vem1(1'b0), .Vai1(soma_1_vai1), .BitSaida(out_10));
  Soma soma_2 (.bit1(in_2), .bit2(in_5), .Vem1(soma_1_vai1), .Vai1(soma_2_vai1), .BitSaida(out_9));
  Soma soma_3 (.bit1(in_1), .bit2(in_4), .Vem1(soma_2_vai1), .Vai1(out_7), .BitSaida(out_8));
  _7_Segment_Display u_7_segment_display_1 (
    .g(\mm_1_saída ), .f(\ec_1_saída ), .a(\mc_1_saída ), .b(\dc_1_saída ), .e(\eb_1_saída ),
    .d(\mb_1_saída ), .c(db_1_out_5));  // open: dp
  _7_Segment_Display u_7_segment_display_2 (
    .g(\mm_2_saída ), .f(\ec_2_saída ), .a(\mc_2_saída ), .b(\dc_2_saída ), .e(\eb_2_saída ),
    .d(\mb_2_saída ), .c(db_2_out_5));  // open: dp
  DC dc_3 (.A(out_7), .B(out_8), .C(out_9), .D(out_10), .\Saída (\dc_3_saída ));
  MC mc_3 (.A(out_7), .B(out_8), .C(out_9), .D(out_10), .\Saída (\mc_3_saída ));
  EC ec_3 (.A(out_7), .B(out_8), .C(out_9), .D(out_10), .\Saída (\ec_3_saída ));
  MM mm_3 (.A(out_7), .B(out_8), .C(out_9), .D(out_10), .\Saída (\mm_3_saída ));
  EB eb_3 (.A(out_7), .B(out_8), .C(out_9), .D(out_10), .\Saída (\eb_3_saída ));
  MB mb_3 (.A(out_7), .B(out_8), .C(out_9), .D(out_10), .\Saída (\mb_3_saída ));
  DB db_3 (.A(out_7), .B(out_8), .C(out_9), .D(out_10), .out_5(db_3_out_5));
  Dezenas dezenas_1 (.A(out_7), .B(out_8), .C(out_9), .\Saída (\dezenas_1_saída ));
  _7_Segment_Display u_7_segment_display_3 (.b(\dezenas_1_saída ), .c(\dezenas_1_saída ));  // open: g, f, a, e, d, dp
  _7_Segment_Display u_7_segment_display_4 (
    .g(\mm_3_saída ), .f(\ec_3_saída ), .a(\mc_3_saída ), .b(\dc_3_saída ), .e(\eb_3_saída ),
    .d(\mb_3_saída ), .c(db_3_out_5));  // open: dp
endmodule

module Soma (
  input  bit1,
  input  bit2,
  input  Vem1,
  output Vai1,
  output BitSaida
);

  wire and_1_out, and_2_out, and_3_out, and_4_out, and_5_out, and_6_out, and_7_out, and_8_out, and_9_out,
       and_10_out, and_11_out, not_1_out, not_2_out, not_3_out, not_4_out, not_5_out, not_6_out, or_1_out,
       or_3_out, or_4_out;

  not not_1 (not_1_out, bit1);
  not not_2 (not_2_out, bit2);
  not not_3 (not_3_out, bit1);
  not not_4 (not_4_out, Vem1);
  not not_5 (not_5_out, bit2);
  not not_6 (not_6_out, Vem1);
  and and_1 (and_1_out, bit1, bit2);
  or or_1 (or_1_out, and_1_out, and_2_out);
  and and_2 (and_2_out, bit1, Vem1);
  and and_3 (and_3_out, bit2, Vem1);
  and and_4 (and_4_out, not_1_out, not_2_out);
  and and_5 (and_5_out, and_4_out, Vem1);
  and and_6 (and_6_out, not_3_out, bit2);
  and and_7 (and_7_out, and_6_out, not_4_out);
  and and_8 (and_8_out, bit1, bit2);
  and and_9 (and_9_out, and_8_out, Vem1);
  and and_10 (and_10_out, bit1, not_5_out);
  and and_11 (and_11_out, and_10_out, not_6_out);
  or or_2 (Vai1, or_1_out, and_3_out);
  or or_3 (or_3_out, and_5_out, and_7_out);
  or or_4 (or_4_out, or_3_out, and_9_out);
  or or_5 (BitSaida, or_4_out, and_11_out);
endmodule

module DB (
  input  A,
  input  B,
  input  C,
  input  D,
  output out_5
);

  wire and_1_out, and_2_out, and_3_out, not_1_out, not_2_out, not_3_out, or_1_out, or_2_out;

  not not_1 (not_1_out, B);
  not not_2 (not_2_out, A);
  not not_3 (not_3_out, C);
  and and_1 (and_1_out, A, not_1_out);
  or or_1 (or_1_out, and_1_out, and_2_out);
  and and_2 (and_2_out, not_2_out, not_3_out);
  and and_3 (and_3_out, B, C);
  or or_2 (or_2_out, or_1_out, and_3_out);
  or or_3 (out_5, or_2_out, D);
endmodule

module DC (
  input  A,
  input  B,
  input  C,
  input  D,
  output \Saída 
);

  wire and_1_out, and_2_out, and_3_out, and_4_out, and_5_out, not_1_out, not_2_out, not_3_out, not_4_out,
       not_5_out, not_6_out, or_1_out, or_2_out, or_3_out;

  not not_1 (not_1_out, A);
  not not_2 (not_2_out, C);
  not not_3 (not_3_out, D);
  not not_4 (not_4_out, C);
  not not_5 (not_5_out, D);
  not not_6 (not_6_out, B);
  and and_1 (and_1_out, not_1_out, C);
  and and_2 (and_2_out, and_1_out, D);
  and and_3 (and_3_out, A, not_2_out);
  and and_4 (and_4_out, A, not_3_out);
  and and_5 (and_5_out, not_4_out, not_5_out);
  or or_1 (or_1_out, and_2_out, and_3_out);
  or or_2 (or_2_out, or_1_out, and_4_out);
  or or_3 (or_3_out, or_2_out, and_5_out);
  or or_4 (\Saída , or_3_out, not_6_out);
endmodule

module EB (
  input  A,
  input  B,
  input  C,
  input  D,
  output \Saída 
);

  wire and_1_out, and_2_out, and_3_out, and_4_out, and_5_out, not_1_out, not_2_out, not_3_out, not_4_out,
       not_5_out, not_6_out, or_1_out;

  not not_1 (not_1_out, A);
  not not_2 (not_2_out, D);
  not not_3 (not_3_out, C);
  not not_4 (not_4_out, D);
  not not_5 (not_5_out, B);
  not not_6 (not_6_out, D);
  and and_1 (and_1_out, not_1_out, C);
  and and_2 (and_2_out, A, not_3_out);
  and and_3 (and_3_out, not_5_out, not_6_out);
  and and_4 (and_4_out, and_1_out, not_2_out);
  and and_5 (and_5_out, and_2_out, not_4_out);
  or or_1 (or_1_out, and_4_out, and_5_out);
  or or_2 (\Saída , or_1_out, and_3_out);
endmodule

module EC (
  input  A,
  input  B,
  input  C,
  input  D,
  output \Saída 
);

  wire and_1_out, and_2_out, and_3_out, and_4_out, and_5_out, and_6_out, and_7_out, and_8_out, and_9_out,
       and_10_out, and_11_out, and_12_out, not_1_out, not_2_out, not_3_out, not_4_out, not_5_out, not_6_out,
       not_7_out, not_8_out, not_9_out, or_1_out, or_2_out, or_3_out, or_4_out;

  not not_1 (not_1_out, A);
  and and_1 (and_1_out, not_1_out, B);
  not not_2 (not_2_out, C);
  and and_2 (and_2_out, A, B);
  and and_3 (and_3_out, A, not_3_out);
  not not_3 (not_3_out, B);
  not not_4 (not_4_out, C);
  and and_4 (and_4_out, A, C);
  not not_5 (not_5_out, D);
  not not_6 (not_6_out, B);
  and and_5 (and_5_out, not_6_out, not_7_out);
  not not_7 (not_7_out, C);
  not not_8 (not_8_out, D);
  and and_6 (and_6_out, B, C);
  not not_9 (not_9_out, D);
  and and_7 (and_7_out, and_1_out, not_2_out);
  and and_8 (and_8_out, and_2_out, C);
  and and_9 (and_9_out, and_3_out, not_4_out);
  and and_10 (and_10_out, and_4_out, not_5_out);
  and and_11 (and_11_out, and_5_out, not_8_out);
  and and_12 (and_12_out, and_6_out, not_9_out);
  or or_1 (or_1_out, and_7_out, and_8_out);
  or or_2 (or_2_out, or_1_out, and_9_out);
  or or_3 (or_3_out, or_2_out, and_10_out);
  or or_4 (or_4_out, or_3_out, and_11_out);
  or or_5 (\Saída , or_4_out, and_12_out);
endmodule

module MB (
  input  A,
  input  B,
  input  C,
  input  D,
  output \Saída 
);

  wire and_1_out, and_2_out, and_3_out, and_4_out, and_5_out, and_6_out, and_7_out, and_8_out, and_9_out,
       and_10_out, not_1_out, not_2_out, not_3_out, not_4_out, not_5_out, not_6_out, not_7_out, not_8_out,
       or_1_out, or_2_out, or_3_out, or_4_out;

  not not_1 (not_1_out, C);
  not not_2 (not_2_out, A);
  not not_3 (not_3_out, D);
  not not_4 (not_4_out, A);
  not not_5 (not_5_out, B);
  not not_6 (not_6_out, B);
  not not_7 (not_7_out, D);
  not not_8 (not_8_out, C);
  and and_1 (and_1_out, A, not_1_out);
  and and_2 (and_2_out, not_2_out, C);
  and and_3 (and_3_out, A, B);
  and and_4 (and_4_out, not_4_out, not_5_out);
  and and_5 (and_5_out, not_6_out, not_7_out);
  and and_6 (and_6_out, B, not_8_out);
  or or_1 (or_1_out, and_1_out, and_7_out);
  and and_7 (and_7_out, and_2_out, not_3_out);
  and and_8 (and_8_out, and_3_out, D);
  and and_9 (and_9_out, and_4_out, C);
  and and_10 (and_10_out, and_6_out, D);
  or or_2 (or_2_out, or_1_out, and_8_out);
  or or_3 (or_3_out, or_2_out, and_9_out);
  or or_4 (or_4_out, or_3_out, and_5_out);
  or or_5 (\Saída , or_4_out, and_10_out);
endmodule

module MM (
  input  A,
  input  B,
  input  C,
  input  D,
  output \Saída 
);

  wire and_1_out, and_2_out, and_3_out, and_4_out, and_5_out, and_6_out, not_1_out, not_2_out, not_3_out,
       not_4_out, not_5_out, or_1_out, or_2_out, or_3_out;

  not not_1 (not_1_out, C);
  not not_2 (not_2_out, A);
  not not_3 (not_3_out, B);
  not not_4 (not_4_out, C);
  not not_5 (not_5_out, D);
  and and_1 (and_1_out, A, B);
  and and_2 (and_2_out, A, not_1_out);
  and and_3 (and_3_out, not_2_out, not_3_out);
  and and_4 (and_4_out, B, not_4_out);
  and and_5 (and_5_out, B, not_5_out);
  or or_1 (or_1_out, and_1_out, and_2_out);
  and and_6 (and_6_out, and_3_out, C);
  or or_2 (or_2_out, or_1_out, and_6_out);
  or or_3 (or_3_out, or_2_out, and_4_out);
  or or_4 (\Saída , or_3_out, and_5_out);
endmodule

module MC (
  input  A,
  input  B,
  input  C,
  input  D,
  output \Saída 
);

  wire and_1_out, and_2_out, and_3_out, and_4_out, not_1_out, not_2_out, not_3_out, not_4_out, or_1_out,
       or_2_out;

  and and_1 (and_1_out, A, not_1_out);
  not not_1 (not_1_out, C);
  not not_2 (not_2_out, A);
  and and_2 (and_2_out, not_2_out, C);
  and and_3 (and_3_out, B, D);
  not not_3 (not_3_out, B);
  and and_4 (and_4_out, not_3_out, not_4_out);
  not not_4 (not_4_out, D);
  or or_1 (or_1_out, and_1_out, and_2_out);
  or or_2 (or_2_out, or_1_out, and_3_out);
  or or_3 (\Saída , or_2_out, and_4_out);
endmodule

module Dezenas (
  input  A,
  input  B,
  input  C,
  output \Saída 
);

  wire and_1_out, and_2_out;

  and and_1 (and_1_out, A, B);
  and and_2 (and_2_out, A, C);
  or or_1 (\Saída , and_1_out, and_2_out);
endmodule
