// Logisim project Teste.circ as structural Verilog: 1 circuit, main circuit main
module main (
  input  in_1,
  input  in_2,
  input  in_3,
  input  in_4,
  input  in_5,
  input  in_6,
  input  in_7,
  input  in_8,
  input  in_9,
  input  in_10,
  input  in_11,
  input  in_12,
  input  in_13,
  input  in_14,
  input  in_15,
  input  in_16,
  input  in_17,
  input  RD,
  input  OE,
  output out_20,
  output out_21,
  output out_22,
  output out_23,
  output out_24,
  output out_25,
  output out_26,
  output out_27,
  output out_28,
  output out_29,
  output out_30,
  output out_31,
  output out_32,
  output out_33,
  output out_34,
  output out_35
);

  wire and_1_out, and_2_out, and_3_out, and_4_out, and_5_out, and_6_out, and_7_out, and_8_out, and_9_out,
       and_10_out, and_11_out, and_12_out, and_13_out, and_14_out, and_15_out, and_16_out, and_17_out,
       and_18_out, and_19_out, and_20_out, and_21_out, and_22_out, and_23_out, and_24_out, and_25_out,
       and_26_out, and_27_out, and_28_out, and_29_out, clock_1_out, clock_2_out, clock_3_out, d_ff_9_q,
       d_ff_10_q, d_ff_11_q, d_ff_12_q, d_ff_13_q, d_ff_14_q, d_ff_15_q, d_ff_16_q, d_ff_17_q, d_ff_18_q,
       d_ff_19_q, d_ff_20_q, d_ff_21_q, d_ff_22_q, d_ff_23_q, d_ff_24_q, not_3_out, not_4_out, not_5_out,
       not_6_out, not_7_out, not_8_out, or_1_out, or_2_out, or_3_out, or_4_out, or_5_out, or_6_out, or_7_out,
       or_8_out, or_9_out, or_10_out, or_11_out, or_12_out, or_13_out, or_14_out, or_15_out, or_16_out;

  Clock clock_1 (.out(clock_1_out));
  D_Flip_Flop d_ff_1 (.clk(clock_1_out), .D(in_3), .Q(out_20));  // open: Qn, preset, en, reset
  D_Flip_Flop d_ff_2 (.clk(clock_1_out), .D(in_4), .Q(out_23));  // open: Qn, preset, en, reset
  D_Flip_Flop d_ff_3 (.clk(clock_1_out), .D(in_6), .Q(out_25));  // open: Qn, preset, en, reset
  D_Flip_Flop d_ff_4 (.clk(clock_1_out), .D(in_7), .Q(out_27));  // open: Qn, preset, en, reset
  D_Flip_Flop d_ff_5 (.clk(clock_1_out), .D(in_8), .Q(out_28));  // open: Qn, preset, en, reset
  D_Flip_Flop d_ff_6 (.clk(clock_1_out), .D(in_9), .Q(out_29));  // open: Qn, preset, en, reset
  D_Flip_Flop d_ff_7 (.clk(clock_1_out), .D(in_10), .Q(out_30));  // open: Qn, preset, en, reset
  D_Flip_Flop d_ff_8 (.clk(clock_1_out), .D(in_11), .Q(out_31));  // open: Qn, preset, en, reset
  not not_1 (out_21, or_1_out);
  or or_1 (or_1_out, in_1, out_24);
  or or_2 (or_2_out, out_21, in_5);
  not not_2 (out_24, or_2_out);
  Clock clock_2 (.out(clock_2_out));
  assign out_33 = and_2_out ? or_10_out : 1'bz;  // Controlled_Buffer controlled_buffer_1
  assign out_34 = and_2_out ? or_13_out : 1'bz;  // Controlled_Buffer controlled_buffer_2
  assign out_35 = and_2_out ? or_16_out : 1'bz;  // Controlled_Buffer controlled_buffer_3
  and and_1 (and_1_out, OE, RD);
  assign out_32 = and_2_out ? or_7_out : 1'bz;  // Controlled_Buffer controlled_buffer_4
  not not_3 (not_3_out, in_16);
  not not_4 (not_4_out, in_17);
  not not_5 (not_5_out, in_17);
  not not_6 (not_6_out, in_16);
  not not_7 (not_7_out, RD);
  and and_2 (and_2_out, and_1_out, clock_2_out);
  and and_3 (and_3_out, not_3_out, not_4_out);
  and and_4 (and_4_out, in_16, not_5_out);
  and and_5 (and_5_out, not_6_out, in_17);
  and and_6 (and_6_out, in_16, in_17);
  and and_7 (and_7_out, clock_2_out, not_7_out);
  Clock clock_3 (.out(clock_3_out));
  not not_8 (not_8_out, in_2);
  and and_8 (and_8_out, and_3_out, and_7_out);
  and and_9 (and_9_out, and_4_out, and_7_out);
  and and_10 (and_10_out, and_5_out, and_7_out);
  and and_11 (and_11_out, and_6_out, and_7_out);
  and and_12 (and_12_out, in_2, clock_3_out);
  or or_3 (or_3_out, and_12_out, out_26);
  or or_4 (or_4_out, out_22, and_13_out);
  and and_13 (and_13_out, clock_3_out, not_8_out);
  not not_9 (out_22, or_3_out);
  not not_10 (out_26, or_4_out);
  D_Flip_Flop d_ff_9 (.clk(and_8_out), .D(in_15), .Q(d_ff_9_q));  // open: Qn, preset, en, reset
  D_Flip_Flop d_ff_10 (.clk(and_9_out), .D(in_15), .Q(d_ff_10_q));  // open: Qn, preset, en, reset
  D_Flip_Flop d_ff_11 (.clk(and_10_out), .D(in_15), .Q(d_ff_11_q));  // open: Qn, preset, en, reset
  D_Flip_Flop d_ff_12 (.clk(and_11_out), .D(in_15), .Q(d_ff_12_q));  // open: Qn, preset, en, reset
  D_Flip_Flop d_ff_13 (.clk(and_8_out), .D(in_14), .Q(d_ff_13_q));  // open: Qn, preset, en, reset
  D_Flip_Flop d_ff_14 (.clk(and_9_out), .D(in_14), .Q(d_ff_14_q));  // open: Qn, preset, en, reset
  D_Flip_Flop d_ff_15 (.clk(and_10_out), .D(in_14), .Q(d_ff_15_q));  // open: Qn, preset, en, reset
  D_Flip_Flop d_ff_16 (.clk(and_11_out), .D(in_14), .Q(d_ff_16_q));  // open: Qn, preset, en, reset
  D_Flip_Flop d_ff_17 (.clk(and_8_out), .D(in_13), .Q(d_ff_17_q));  // open: Qn, preset, en, reset
  D_Flip_Flop d_ff_18 (.clk(and_9_out), .D(in_13), .Q(d_ff_18_q));  // open: Qn, preset, en, reset
  D_Flip_Flop d_ff_19 (.clk(and_10_out), .D(in_13), .Q(d_ff_19_q));  // open: Qn, preset, en, reset
  D_Flip_Flop d_ff_20 (.clk(and_11_out), .D(in_13), .Q(d_ff_20_q));  // open: Qn, preset, en, reset
  D_Flip_Flop d_ff_21 (.clk(and_8_out), .D(in_12), .Q(d_ff_21_q));  // open: Qn, preset, en, reset
  D_Flip_Flop d_ff_22 (.clk(and_9_out), .D(in_12), .Q(d_ff_22_q));  // open: Qn, preset, en, reset
  D_Flip_Flop d_ff_23 (.clk(and_10_out), .D(in_12), .Q(d_ff_23_q));  // open: Qn, preset, en, reset
  D_Flip_Flop d_ff_24 (.clk(and_11_out), .D(in_12), .Q(d_ff_24_q));  // open: Qn, preset, en, reset
  and and_14 (and_14_out, and_4_out, d_ff_10_q);
  and and_15 (and_15_out, and_3_out, d_ff_9_q);
  or or_5 (or_5_out, and_15_out, and_14_out);
  and and_16 (and_16_out, and_5_out, d_ff_11_q);
  or or_6 (or_6_out, or_5_out, and_16_out);
  and and_17 (and_17_out, and_6_out, d_ff_12_q);
  or or_7 (or_7_out, or_6_out, and_17_out);
  and and_18 (and_18_out, and_3_out, d_ff_13_q);
  or or_8 (or_8_out, and_18_out, and_19_out);
  and and_19 (and_19_out, and_4_out, d_ff_14_q);
  and and_20 (and_20_out, and_5_out, d_ff_15_q);
  or or_9 (or_9_out, or_8_out, and_20_out);
  and and_21 (and_21_out, and_6_out, d_ff_16_q);
  or or_10 (or_10_out, or_9_out, and_21_out);
  and and_22 (and_22_out, and_3_out, d_ff_17_q);
  and and_23 (and_23_out, and_4_out, d_ff_18_q);
  or or_11 (or_11_out, and_22_out, and_23_out);
  or or_12 (or_12_out, or_11_out, and_25_out);
  and and_24 (and_24_out, and_6_out, d_ff_20_q);
  and and_25 (and_25_out, and_5_out, d_ff_19_q);
  or or_13 (or_13_out, or_12_out, and_24_out);
  and and_26 (and_26_out, and_3_out, d_ff_21_q);
  and and_27 (and_27_out, and_4_out, d_ff_22_q);
  or or_14 (or_14_out, and_26_out, and_27_out);
  and and_28 (and_28_out, and_5_out, d_ff_23_q);
  or or_15 (or_15_out, or_14_out, and_28_out);
  or or_16 (or_16_out, or_15_out, and_29_out);
  and and_29 (and_29_out, and_6_out, d_ff_24_q);
endmodule
